// Logisim project processor.circ as structural Verilog
module register_file (
  input  clock,
  input  [4:0] ID_Ra,
  input  register_write_enable,
  input  [4:0] ID_Rb,
  input  [31:0] R_in,
  input  clear_registers,
  input  [4:0] ID_Rc,
  output [31:0] RA,
  output [31:0] RB
);

  wire R0_en, R1_en, R2_en, R3_en, R4_en, R5_en, R6_en, R7_en, R8_en, R9_en, R10_en, R11_en, R12_en, R13_en,
       R14_en, R15_en, R16_en, R17_en, R18_en, R19_en, R20_en, R21_en, R22_en, R23_en, R24_en, R25_en,
       R26_en, R27_en, R28_en, R29_en, R30_en, R31_en;
  wire [31:0] R0_out, R1_out, R2_out, R3_out, R4_out, R5_out, R6_out, R7_out, R8_out, R9_out, R10_out,
       R11_out, R12_out, R13_out, R14_out, R15_out, R16_out, R17_out, R18_out, R19_out, R20_out, R21_out,
       R22_out, R23_out, R24_out, R25_out, R26_out, R27_out, R28_out, R29_out, R30_out, R31_out;

  Register #(.width(32)) register_1 (.D(R_in), .en(R0_en), .Q(R0_out), .clk(clock), .clr(clear_registers));
  Register #(.width(32)) register_2 (.D(R_in), .en(R4_en), .Q(R4_out), .clk(clock), .clr(clear_registers));
  Register #(.width(32)) register_3 (.D(R_in), .en(R8_en), .Q(R8_out), .clk(clock), .clr(clear_registers));
  Register #(.width(32)) register_4 (.D(R_in), .en(R12_en), .Q(R12_out), .clk(clock), .clr(clear_registers));
  Register #(.width(32)) register_5 (.D(R_in), .en(R16_en), .Q(R16_out), .clk(clock), .clr(clear_registers));
  Register #(.width(32)) register_6 (.D(R_in), .en(R20_en), .Q(R20_out), .clk(clock), .clr(clear_registers));
  Register #(.width(32)) register_7 (.D(R_in), .en(R24_en), .Q(R24_out), .clk(clock), .clr(clear_registers));
  Register #(.width(32)) register_8 (.D(R_in), .en(R28_en), .Q(R28_out), .clk(clock), .clr(clear_registers));
  Register #(.width(32)) register_9 (.D(R_in), .en(R1_en), .Q(R1_out), .clk(clock), .clr(clear_registers));
  Register #(.width(32)) register_10 (.D(R_in), .en(R5_en), .Q(R5_out), .clk(clock), .clr(clear_registers));
  Register #(.width(32)) register_11 (.D(R_in), .en(R9_en), .Q(R9_out), .clk(clock), .clr(clear_registers));
  Register #(.width(32)) register_12 (.D(R_in), .en(R13_en), .Q(R13_out), .clk(clock), .clr(clear_registers));
  Register #(.width(32)) register_13 (.D(R_in), .en(R17_en), .Q(R17_out), .clk(clock), .clr(clear_registers));
  Register #(.width(32)) register_14 (.D(R_in), .en(R21_en), .Q(R21_out), .clk(clock), .clr(clear_registers));
  Register #(.width(32)) register_15 (.D(R_in), .en(R25_en), .Q(R25_out), .clk(clock), .clr(clear_registers));
  Register #(.width(32)) register_16 (.D(R_in), .en(R29_en), .Q(R29_out), .clk(clock), .clr(clear_registers));
  Register #(.width(32)) register_17 (.D(R_in), .en(R2_en), .Q(R2_out), .clk(clock), .clr(clear_registers));
  Register #(.width(32)) register_18 (.D(R_in), .en(R6_en), .Q(R6_out), .clk(clock), .clr(clear_registers));
  Register #(.width(32)) register_19 (.D(R_in), .en(R10_en), .Q(R10_out), .clk(clock), .clr(clear_registers));
  Register #(.width(32)) register_20 (.D(R_in), .en(R14_en), .Q(R14_out), .clk(clock), .clr(clear_registers));
  Register #(.width(32)) register_21 (.D(R_in), .en(R18_en), .Q(R18_out), .clk(clock), .clr(clear_registers));
  Register #(.width(32)) register_22 (.D(R_in), .en(R22_en), .Q(R22_out), .clk(clock), .clr(clear_registers));
  Register #(.width(32)) register_23 (.D(R_in), .en(R26_en), .Q(R26_out), .clk(clock), .clr(clear_registers));
  Register #(.width(32)) register_24 (.D(R_in), .en(R30_en), .Q(R30_out), .clk(clock), .clr(clear_registers));
  Register #(.width(32)) register_25 (.D(R_in), .en(R3_en), .Q(R3_out), .clk(clock), .clr(clear_registers));
  Register #(.width(32)) register_26 (.D(R_in), .en(R7_en), .Q(R7_out), .clk(clock), .clr(clear_registers));
  Register #(.width(32)) register_27 (.D(R_in), .en(R11_en), .Q(R11_out), .clk(clock), .clr(clear_registers));
  Register #(.width(32)) register_28 (.D(R_in), .en(R15_en), .Q(R15_out), .clk(clock), .clr(clear_registers));
  Register #(.width(32)) register_29 (.D(R_in), .en(R19_en), .Q(R19_out), .clk(clock), .clr(clear_registers));
  Register #(.width(32)) register_30 (.D(R_in), .en(R23_en), .Q(R23_out), .clk(clock), .clr(clear_registers));
  Register #(.width(32)) register_31 (.D(R_in), .en(R27_en), .Q(R27_out), .clk(clock), .clr(clear_registers));
  Register #(.width(32)) register_32 (.D(R_in), .en(R31_en), .Q(R31_out), .clk(clock), .clr(clear_registers));
  // Probe on R0_out
  // Probe on R1_out
  // Probe on R2_out
  // Probe on R3_out
  // Probe on R4_out
  // Probe on R5_out
  // Probe on R6_out
  // Probe on R7_out
  // Probe on R8_out
  // Probe on R9_out
  // Probe on R10_out
  // Probe on R11_out
  // Probe on R12_out
  // Probe on R13_out
  // Probe on R14_out
  // Probe on R15_out
  Multiplexer #(.select(5), .width(32), .enable("false")) multiplexer_1 (
    .in0(R0_out), .in1(R1_out), .in2(R2_out), .in3(R3_out), .in4(R4_out), .in5(R5_out), .in6(R6_out),
    .in7(R7_out), .in8(R8_out), .in9(R9_out), .in10(R10_out), .in11(R11_out), .in12(R12_out), .in13(R13_out),
    .in14(R14_out), .in15(R15_out), .in16(R16_out), .in17(R17_out), .in18(R18_out), .in19(R19_out),
    .in20(R20_out), .in21(R21_out), .in22(R22_out), .in23(R23_out), .in24(R24_out), .in25(R25_out),
    .in26(R26_out), .in27(R27_out), .in28(R28_out), .in29(R29_out), .in30(R30_out), .in31(R31_out), .out(RA),
    .sel(ID_Ra));
  Demultiplexer #(.select(5), .enable("false")) demultiplexer_1 (
    .out0(R0_en), .out1(R1_en), .out2(R2_en), .out3(R3_en), .out4(R4_en), .out5(R5_en), .out6(R6_en),
    .out7(R7_en), .out8(R8_en), .out9(R9_en), .out10(R10_en), .out11(R11_en), .out12(R12_en), .out13(R13_en),
    .out14(R14_en), .out15(R15_en), .out16(R16_en), .out17(R17_en), .out18(R18_en), .out19(R19_en),
    .out20(R20_en), .out21(R21_en), .out22(R22_en), .out23(R23_en), .out24(R24_en), .out25(R25_en),
    .out26(R26_en), .out27(R27_en), .out28(R28_en), .out29(R29_en), .out30(R30_en), .out31(R31_en),
    .in(register_write_enable), .sel(ID_Rc));
  // Probe on R16_out
  // Probe on R17_out
  // Probe on R18_out
  // Probe on R19_out
  // Probe on R20_out
  // Probe on R21_out
  // Probe on R22_out
  // Probe on R23_out
  // Probe on R24_out
  // Probe on R25_out
  // Probe on R26_out
  // Probe on R27_out
  // Probe on R28_out
  // Probe on R29_out
  // Probe on R30_out
  // Probe on R31_out
  Multiplexer #(.select(5), .width(32), .enable("false")) multiplexer_2 (
    .in0(R0_out), .in1(R1_out), .in2(R2_out), .in3(R3_out), .in4(R4_out), .in5(R5_out), .in6(R6_out),
    .in7(R7_out), .in8(R8_out), .in9(R9_out), .in10(R10_out), .in11(R11_out), .in12(R12_out), .in13(R13_out),
    .in14(R14_out), .in15(R15_out), .in16(R16_out), .in17(R17_out), .in18(R18_out), .in19(R19_out),
    .in20(R20_out), .in21(R21_out), .in22(R22_out), .in23(R23_out), .in24(R24_out), .in25(R25_out),
    .in26(R26_out), .in27(R27_out), .in28(R28_out), .in29(R29_out), .in30(R30_out), .in31(R31_out), .out(RB),
    .sel(ID_Rb));

  // Other names for the same wires on the sheet: clear = clear_registers; clk = clock;
  //   write_en = register_write_enable
endmodule

module ALU (
  input  [31:0] Input_1,
  input  [31:0] Input_2,
  input  [1:0] Opeartion_selector,
  output [31:0] Output
);

  wire [31:0] adder_1_out, and_1_out, or_1_out, subtractor_1_out;

  Adder #(.width(32)) adder_1 (.a(Input_1), .b(Input_2), .out(adder_1_out));  // open: cin, cout
  Subtractor #(.width(32)) subtractor_1 (.a(Input_1), .b(Input_2), .out(subtractor_1_out));  // open: bin, bout
  assign and_1_out = Input_1 & Input_2;  // AND_Gate and_1, 32 bits wide
  assign or_1_out = Input_1 | Input_2;  // OR_Gate or_1, 32 bits wide
  Multiplexer #(.select(2), .width(32), .enable("false")) multiplexer_1 (
    .in0(adder_1_out), .in1(subtractor_1_out), .in2(and_1_out), .in3(or_1_out), .out(Output),
    .sel(Opeartion_selector));

  // Other names for the same wires on the sheet: alu_output[31:0] = Output; op_selector[1:0] = Opeartion_selector
endmodule
